// Logisim project Full Project Final .circ as structural Verilog: 8 circuits, main circuit Add & Sub
module Add___Sub (
  input  Sign_A,
  input  A1,
  input  A0,
  input  Add_0_Sub_1,
  input  Sign_B,
  input  B1,
  input  B0,
  output Sign,
  output S2,
  output S1,
  output S0,
  output Zero_Flag
);

  wire add_1_carry_sign, add_1_s0, add_1_s1, add_1_s2, signed_to_2_s_complement_3_bits_1_sign_y,
       signed_to_2_s_complement_3_bits_1_y0, signed_to_2_s_complement_3_bits_1_y1,
       signed_to_2_s_complement_3_bits_2_sign_y, signed_to_2_s_complement_3_bits_2_y0,
       signed_to_2_s_complement_3_bits_2_y1, xor_1_sign_y, xor_1_y0, xor_1_y1, xor_2_out, xor_3_out,
       xor_4_out;

  Signed_to_2_s_Complement__3_bits signed_to_2_s_complement_3_bits_1 (
    .Sign_X(Sign_A), .X1(A1), .X0(A0), .Sign_Y(signed_to_2_s_complement_3_bits_1_sign_y),
    .Y1(signed_to_2_s_complement_3_bits_1_y1), .Y0(signed_to_2_s_complement_3_bits_1_y0));
  ADD add_1 (
    .B1(xor_1_y1), .A1(signed_to_2_s_complement_3_bits_1_y1), .Sign_B(xor_1_sign_y),
    .Sign_A(signed_to_2_s_complement_3_bits_1_sign_y), .Sum_0_Sub_1(Add_0_Sub_1),
    .A0(signed_to_2_s_complement_3_bits_1_y0), .B0(xor_1_y0), .Carry_Sign(add_1_carry_sign), .S2(add_1_s2),
    .S1(add_1_s1), .S0(add_1_s0));
  Signed_to_2_s_Complement__3_bits signed_to_2_s_complement_3_bits_2 (
    .Sign_X(Sign_B), .X1(B1), .X0(B0), .Sign_Y(signed_to_2_s_complement_3_bits_2_sign_y),
    .Y1(signed_to_2_s_complement_3_bits_2_y1), .Y0(signed_to_2_s_complement_3_bits_2_y0));
  XOR xor_1 (
    .Sign_X(signed_to_2_s_complement_3_bits_2_sign_y), .X1(signed_to_2_s_complement_3_bits_2_y1),
    .X0(signed_to_2_s_complement_3_bits_2_y0), .Sum_0_Sub_1(Add_0_Sub_1), .Sign_Y(xor_1_sign_y),
    .Y1(xor_1_y1), .Y0(xor_1_y0));
  xor xor_2 (xor_2_out, Add_0_Sub_1, signed_to_2_s_complement_3_bits_2_sign_y);
  xor xor_3 (xor_3_out, xor_2_out, signed_to_2_s_complement_3_bits_1_sign_y);
  xor xor_4 (xor_4_out, xor_3_out, add_1_carry_sign);
  nor nor_1 (Zero_Flag, S2, S1, S0);
  Signed_to_2_s_Complement__4_bits signed_to_2_s_complement_4_bits_1 (
    .Sign(xor_4_out), .X(add_1_s2), .Y(add_1_s1), .Z(add_1_s0), .Sign_2(Sign), .S2(S2), .S1(S1), .S0(S0));

  // Notes on the sheet:
  //   =
endmodule

// Signed to 2's Complement
module Signed_to_2_s_Complement__3_bits (
  input  Sign_X,
  input  X1,
  input  X0,
  output Sign_Y,
  output Y1,
  output Y0
);

  wire and_1_out, and_3_out, and_4_out, not_1_out, not_2_out, not_3_out, or_1_out, or_2_out;

  not not_1 (not_1_out, Sign_X);
  not not_2 (not_2_out, X1);
  not not_3 (not_3_out, X0);
  or or_1 (or_1_out, X0, X1);
  and and_1 (and_1_out, X0, not_2_out);
  or or_2 (or_2_out, not_3_out, not_1_out);
  and and_2 (Sign_Y, or_1_out, Sign_X);
  and and_3 (and_3_out, and_1_out, Sign_X);
  and and_4 (and_4_out, or_2_out, X1);
  or or_3 (Y1, and_3_out, and_4_out);

  assign Y0 = X0;
endmodule

module XOR (
  input  Sign_X,
  input  X1,
  input  X0,
  input  Sum_0_Sub_1,
  output Sign_Y,
  output Y1,
  output Y0
);

  xor xor_1 (Sign_Y, Sign_X, Sum_0_Sub_1);
  xor xor_2 (Y1, X1, Sum_0_Sub_1);
  xor xor_3 (Y0, X0, Sum_0_Sub_1);
endmodule

// Add
module ADD (
  input  Sum_0_Sub_1,
  input  A0,
  input  B0,
  input  B1,
  input  A1,
  input  Sign_B,
  input  Sign_A,
  output Carry_Sign,
  output S2,
  output S1,
  output S0
);

  wire full_adder_1_carry_out, full_adder_2_carry_out;

  Full_Adder full_adder_1 (.Carry_in(Sum_0_Sub_1), .X(A0), .Y(B0), .Sum(S0), .Carry_out(full_adder_1_carry_out));
  Full_Adder full_adder_2 (
    .Carry_in(full_adder_1_carry_out), .X(A1), .Y(B1), .Sum(S1), .Carry_out(full_adder_2_carry_out));
  Full_Adder full_adder_3 (.Carry_in(full_adder_2_carry_out), .X(Sign_A), .Y(Sign_B), .Sum(S2), .Carry_out(Carry_Sign));
endmodule

module Full_Adder (
  input  Carry_in,
  input  X,
  input  Y,
  output Sum,
  output Carry_out
);

  wire and_1_out, and_2_out, xor_1_out;

  xor xor_1 (xor_1_out, Y, X);
  and and_1 (and_1_out, Y, X);
  xor xor_2 (Sum, xor_1_out, Carry_in);
  and and_2 (and_2_out, Carry_in, xor_1_out);
  or or_1 (Carry_out, and_1_out, and_2_out);
endmodule

// Signed to 2's Complement
module Signed_to_2_s_Complement__4_bits (
  input  Sign,
  input  X,
  input  Y,
  input  Z,
  output Sign_2,
  output S2,
  output S1,
  output S0
);

  wire and_1_out, and_2_out, and_3_out, and_4_out, not_1_out, not_2_out, not_3_out, xor_1_out, xor_2_out;

  not not_1 (not_1_out, Sign);
  not not_2 (not_2_out, Y);
  not not_3 (not_3_out, Z);
  and and_1 (and_1_out, not_2_out, Sign);
  and and_2 (and_2_out, Y, not_1_out);
  xor xor_1 (xor_1_out, Y, Z);
  xor xor_2 (xor_2_out, X, Sign);
  and and_3 (and_3_out, not_3_out, and_1_out);
  and and_4 (and_4_out, Sign, xor_1_out);
  or or_1 (S2, xor_2_out, and_3_out);
  or or_2 (S1, and_2_out, and_4_out);

  assign S0 = Z;
  assign Sign_2 = Sign;
endmodule

module ALU (
  input  Sign_A,
  input  A1,
  input  A0,
  input  Sign_B,
  input  B1,
  input  B0,
  input  C1,
  input  C0,
  output Sign,
  output F3,
  output F2,
  output F1,
  output F0,
  output Zero,
  output Div_by_Zero
);

  wire add_sub_1_s0, add_sub_1_s1, add_sub_1_s2, add_sub_1_sign, and_2_out, division_1_c0, division_1_c1,
       division_1_div_by_zero_flag, division_1_sign_flag, multiplication_1_m0, multiplication_1_m1,
       multiplication_1_m2, multiplication_1_m3, multiplication_1_m4, n74153_3__7__y1, nor_1_out, not_1_out,
       not_2_out;

  Division division_1 (
    .B0(B0), .B1(B1), .A0(A0), .A1(A1), .A2_Sign(Sign_A), .Sign_Flag(division_1_sign_flag),
    .C1(division_1_c1), .C0(division_1_c0), .Div_by_zero_Flag(division_1_div_by_zero_flag));  // open: Zero_Flag
  Add___Sub add_sub_1 (
    .Sign_A(Sign_A), .A1(A1), .A0(A0), .Add_0_Sub_1(C0), .Sign_B(Sign_B), .B1(B1), .B0(B0),
    .Sign(add_sub_1_sign), .S2(add_sub_1_s2), .S1(add_sub_1_s1), .S0(add_sub_1_s0));  // open: Zero_Flag
  Multiplication multiplication_1 (
    .minus_ve(Sign_A), .A1(A1), .A0(A0), .B1(B1), .B0(B0), .minus_ve_2(Sign_B), .M0(multiplication_1_m0),
    .M1(multiplication_1_m1), .M2(multiplication_1_m2), .M3(multiplication_1_m3), .M4(multiplication_1_m4));
  _74153 u_74153_1 (
    ._1__nG1(1'b0), ._2__B(C1), ._3__1C3(division_1_c0), ._4__1C2(multiplication_1_m0),
    ._5__1C1(add_sub_1_s0), ._6__1C0(add_sub_1_s0), ._7__Y1(F0), ._8__GND(1'b0), ._16__Vcc(1'b1),
    ._15__nG2(1'b0), ._14__A(C0), ._13__2C3(division_1_c1), ._12__2C2(multiplication_1_m1),
    ._11__2C1(add_sub_1_s1), ._10__2C0(add_sub_1_s1), ._9__Y2(F1));
  _74153 u_74153_2 (
    ._1__nG1(1'b0), ._2__B(C1), ._3__1C3(1'b0), ._4__1C2(multiplication_1_m2), ._5__1C1(add_sub_1_s2),
    ._6__1C0(add_sub_1_s2), ._7__Y1(F2), ._8__GND(1'b0), ._16__Vcc(1'b1), ._15__nG2(1'b0), ._14__A(C0),
    ._13__2C3(1'b0), ._12__2C2(multiplication_1_m3), ._11__2C1(1'b0), ._10__2C0(1'b0), ._9__Y2(F3));
  _74153 u_74153_3 (
    ._1__nG1(1'b0), ._2__B(C1), ._3__1C3(division_1_sign_flag), ._4__1C2(multiplication_1_m4),
    ._5__1C1(add_sub_1_sign), ._6__1C0(add_sub_1_sign), ._7__Y1(n74153_3__7__y1), ._8__GND(1'b0),
    ._16__Vcc(1'b1), ._15__nG2(1'b0), ._14__A(1'b0), ._13__2C3(1'b0), ._12__2C2(1'b0), ._11__2C1(1'b0),
    ._10__2C0(1'b0));  // open: _9__Y2
  and and_1 (Sign, n74153_3__7__y1, not_1_out);
  not not_1 (not_1_out, nor_1_out);
  and and_2 (and_2_out, C1, C0);
  nor nor_1 (nor_1_out, F3, F2, F1, F0);
  and and_3 (Div_by_Zero, and_2_out, division_1_div_by_zero_flag);
  and and_4 (Zero, nor_1_out, not_2_out);
  not not_2 (not_2_out, Div_by_Zero);
endmodule

module Main (
  input  minus_ve,
  input  A1,
  input  A0,
  input  minus_ve_2,
  input  B1,
  input  B0,
  input  S1,
  input  S0,
  output Zero_Flag,
  output Div_By_Zero,
  output Sign_Flag
);

  wire alu_1_f0, alu_1_f1, alu_1_f2, alu_1_f3, n7448_1__9__e, n7448_1__10__d, n7448_1__11__c, n7448_1__12__b,
       n7448_1__13__a, n7448_1__14__g, n7448_1__15__f, not_1_out;

  ALU alu_1 (
    .Sign_A(minus_ve), .A1(A1), .A0(A0), .Sign_B(minus_ve_2), .B1(B1), .B0(B0), .C1(S1), .C0(S0),
    .Sign(Sign_Flag), .F3(alu_1_f3), .F2(alu_1_f2), .F1(alu_1_f1), .F0(alu_1_f0), .Zero(Zero_Flag),
    .Div_by_Zero(Div_By_Zero));
  not not_1 (not_1_out, Div_By_Zero);
  _7448 u_7448_1 (
    ._1__B(alu_1_f1), ._2__C(alu_1_f2), ._3__nLT(1'b1), ._5__nRBI(not_1_out), ._6__D(alu_1_f3),
    ._7__A(alu_1_f0), ._8__GND(1'b0), ._16__Vcc(1'b1), ._15__f(n7448_1__15__f), ._14__g(n7448_1__14__g),
    ._13__a(n7448_1__13__a), ._12__b(n7448_1__12__b), ._11__c(n7448_1__11__c), ._10__d(n7448_1__10__d),
    ._9__e(n7448_1__9__e));  // open: _4__NC
  _7_Segment_Display u_7_segment_display_1 (.g(Sign_Flag));  // open: f, a, b, e, d, c, dp
  _7_Segment_Display u_7_segment_display_2 (
    .g(n7448_1__14__g), .f(n7448_1__15__f), .a(n7448_1__13__a), .b(n7448_1__12__b), .e(n7448_1__9__e),
    .d(n7448_1__10__d), .c(n7448_1__11__c));  // open: dp

  // Notes on the sheet:
  //   00 Addition
  //   01 Subtraction
  //   10 Multiplication
  //   11 Remainder
endmodule
