// Logisim project HA.circ as structural Verilog: 2 circuits, main circuit HA
module HA (
  input  x,
  input  y,
  output carry,
  output sum
);

  and and_1 (carry, x, y);
  xor xor_1 (sum, x, y);
endmodule

module Multiplier (
  input  A2,
  input  A1,
  input  A0,
  input  B1,
  input  B0,
  input  B2,
  output M0,
  output M1,
  output M3,
  output M2,
  output M4
);

  wire _2_out, _3_out, _4_out, ha_1_carry;

  and _1 (M0, A0, B0);
  and _2 (_2_out, A1, B0);
  and _3 (_3_out, A0, B1);
  and _4 (_4_out, A1, B1);
  HA ha_1 (.x(_2_out), .y(_3_out), .carry(ha_1_carry), .sum(M1));
  HA ha_2 (.x(ha_1_carry), .y(_4_out), .carry(M3), .sum(M2));
  xor xor_1 (M4, A2, B2);
endmodule
