// Logisim project Multiplication.circ as structural Verilog: 1 circuit, main circuit Multiplication
// Mult
module Multiplication (
  input  minus_ve,
  input  A1,
  input  A0,
  input  B1,
  input  B0,
  input  minus_ve_2,
  output M0,
  output M1,
  output M2,
  output M3,
  output M4
);

  wire HA_carry, n7408_1__6__2y, n7408_1__8__3y, n7408_1__11__4y;

  _7408 u_7408_1 (
    ._1__1A(B0), ._2__1B(A0), ._3__1Y(M0), ._4__2A(A1), ._5__2B(B0), ._6__2Y(n7408_1__6__2y), ._7__GND(1'b0),
    ._14__Vcc(1'b1), ._13__4B(A0), ._12__4A(B1), ._11__4Y(n7408_1__11__4y), ._10__3B(A1), ._9__3A(B1),
    ._8__3Y(n7408_1__8__3y));
  HA HA (.x(n7408_1__6__2y), .y(n7408_1__11__4y), .carry(HA_carry), .sum(M1));
  HA HA_2 (.x(HA_carry), .y(n7408_1__8__3y), .carry(M3), .sum(M2));
  _7486 u_7486_1 (
    ._1__1A(minus_ve), ._2__1B(minus_ve_2), ._3__1Y(M4), ._7__GND(1'b0), ._14__Vcc(1'b1));  // open: _4__2A, _5__2B, _6__2Y, _13__4B, _12__4A, _11__4Y, _10__3B, _9__3A, _8__3Y
endmodule
