// Logisim project RemainderFinalEdits.circ as structural Verilog: 1 circuit, main circuit Division
// Div
module Division (
  input  B0,
  input  B1,
  input  A0,
  input  A1,
  input  A2_Sign,
  output Sign_Flag,
  output C1,
  output C0,
  output Zero_Flag,
  output Div_by_zero_Flag
);

  wire AND__3__1y, NAND__3__1y, NOR__13__4y, NOT__2__1y, NOT__8__4y;

  _7421 _4_IN_AND (
    ._1__1A(A1), ._2__1B(B1), ._4__1C(B0), ._5__1D(NOT__2__1y), ._6__1Y(C1), ._7__GND(1'b0), ._14__Vcc(1'b1));  // open: _3__NC, _13__2D, _12__2C, _11__NC, _10__2B, _9__2A, _8__2Y
  _7404 NOT (
    ._1__1A(A0), ._2__1Y(NOT__2__1y), ._7__GND(1'b0), ._14__Vcc(1'b1), ._9__4A(Div_by_zero_Flag),
    ._8__4Y(NOT__8__4y));  // open: _3__2A, _4__2Y, _5__3A, _6__3Y, _13__6A, _12__6Y, _11__5A, _10__5Y
  _7400 NAND (
    ._1__1A(A1), ._2__1B(B0), ._3__1Y(NAND__3__1y), ._7__GND(1'b0), ._14__Vcc(1'b1));  // open: _4__2A, _5__2B, _6__2Y, _13__4B, _12__4A, _11__4Y, _10__3B, _9__3A, _8__3Y
  _7408 AND (
    ._1__1A(A0), ._2__1B(B1), ._3__1Y(AND__3__1y), ._4__2A(AND__3__1y), ._5__2B(NAND__3__1y), ._6__2Y(C0),
    ._7__GND(1'b0), ._14__Vcc(1'b1), ._13__4B(NOT__8__4y), ._12__4A(NOR__13__4y), ._11__4Y(Zero_Flag));  // open: _10__3B, _9__3A, _8__3Y
  _7402 NOR (
    ._1__1Y(Div_by_zero_Flag), ._2__1A(B0), ._3__1B(B1), ._7__GND(1'b0), ._14__Vcc(1'b1),
    ._13__4Y(NOR__13__4y), ._12__4B(C0), ._11__4A(C1));  // open: _4__2Y, _5__2A, _6__2B, _10__3Y, _9__3B, _8__3A

  assign Sign_Flag = A2_Sign;

  // Notes on the sheet:
  //   Inputs
endmodule
